# Fritzing sketch JAMS-Temperature_and_humidity (saved by Fritzing 0.9.3b)
breadboards: 1

parts:
  Part1 = Lithium Ion Battery Pack 3.7V 6600mAh [part_number=353]
  Part2 = Adafruit Feather HUZZAH ESP8266 [part_number="Adafruit #2821"]
  Part3 = Adafruit BME280
  U2 = SIP - 8 pins [chip_label="Sparkfun Fuel Gauge" package="SIP (Single Inline) [THT]"]

nets:
  N1: Part1.positive, U2.+
  N2: Part1.negative, U2.-
  GND: Part2.GND, Part3.GND, U2.GND
  3.3V: Part2.3.3V, Part3.VIN
  N3: Part2.VBAT, U2.VCC
  N4: Part2.GPIO4/SDA, Part3.SDI/SDA

custom parts:
  Lithium Ion Battery Pack 3.7V 6600mAh: This lithium ion pack is made of 3 balanced 2200mAh cells for a total of 6600mA capacity! The cells are connected in parallel and spot-welded to a protection circuit that provides over-voltage, under-voltage and over-current protection. Each cell can provide 0.5C of current (1.1 A per) so all together the peak current you can draw is over 3.3 Amps. Note that these batteries are not designed to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
  Adafruit Feather HUZZAH ESP8266: his is the Adafruit Feather HUZZAH ESP8266 - our take on an 'all-in-one' ESP8266 WiFi development board with built in USB and battery charging. Its an ESP8266 WiFi module with all the extras you need, ready to rock! We have other boards in the Feather family, check'em out here. At the Feather HUZZAH's heart is an ESP8266 WiFi microcontroller clocked at 80 MHz and at 3.3V logic. This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
  Adafruit BME280: Bosch has stepped up their game with their new BME280 sensor, an environmental sensor with temperature, barometric pressure and humidity! This sensor is great for all sorts of weather/environmental sensing and can even be used in both I2C and SPI! This precision sensor from Bosch is the best low-cost sensing solution for measuring humidity with ±3% accuracy, barometric pressure with ±1 hPa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
  SIP - 8 pins: A SIP stand-in part for whatever you want. With 8 pins on a 300 mil single inline package (SIP) footprint.
